# Fritzing sketch Leds Sketch (saved by Fritzing 0.7.12b)
perfboards: 1

parts:
  74HC595 = 74HC595 [package="DIP16 [THT]"]
  LED7 = RGB LED (com. anode, rbg) [package="5 mm [THT]"]
  R16 = Resistor [tolerance=±5% resistance=470 package=THT]
  R17 = Resistor [tolerance=±5% resistance=470 package=THT]
  R18 = Resistor [tolerance=±5% resistance=470 package=THT]
  R19 = Resistor [tolerance=±5% resistance=470 package=THT]
  R20 = Resistor [tolerance=±5% resistance=470 package=THT]
  R43 = Resistor [tolerance=±5% resistance=470 package=THT]
  R25 = Resistor [tolerance=±5% resistance=470 package=THT]
  R26 = Resistor [tolerance=±5% resistance=470 package=THT]
  R27 = Resistor [tolerance=±5% resistance=470 package=THT]
  R28 = Resistor [tolerance=±5% resistance=470 package=THT]
  R29 = Resistor [tolerance=±5% resistance=470 package=THT]
  R30 = Resistor [tolerance=±5% resistance=470 package=THT]
  R31 = Resistor [tolerance=±5% resistance=470 package=THT]
  R32 = Resistor [tolerance=±5% resistance=470 package=THT]
  R33 = Resistor [tolerance=±5% resistance=470 package=THT]
  LED5 = RGB LED (com. anode, rbg) [package="5 mm [THT]"]
  LED6 = RGB LED (com. anode, rbg) [package="5 mm [THT]"]
  LED4 = RGB LED (com. anode, rbg) [package="5 mm [THT]"]
  74HC595_2 = 74HC595 [package="DIP16 [THT]"]
  R34 = Resistor [tolerance=±5% resistance=470 package=THT]
  R35 = Resistor [tolerance=±5% resistance=470 package=THT]
  R36 = Resistor [tolerance=±5% resistance=470 package=THT]
  R37 = Resistor [tolerance=±5% resistance=470 package=THT]
  R38 = Resistor [tolerance=±5% resistance=470 package=THT]
  R39 = Resistor [tolerance=±5% resistance=470 package=THT]
  R40 = Resistor [tolerance=±5% resistance=470 package=THT]
  R41 = Resistor [tolerance=±5% resistance=470 package=THT]
  R42 = Resistor [tolerance=±5% resistance=470 package=THT]
  LED2 = RGB LED (com. anode, rbg) [package="5 mm [THT]"]
  LED3 = RGB LED (com. anode, rbg) [package="5 mm [THT]"]
  LED1 = RGB LED (com. anode, rbg) [package="5 mm [THT]"]
  jumper = male pin header, 3 pins [form="♂ (male)"]
  J2 = male pin header, 2 pins [form="♂ (male)"]
  74HC595_3 = 74HC595 [package="DIP16 [THT]"]
  LED8 = RGB LED (com. anode, rbg) [package="5 mm [THT]"]
  1uF = Electrolytic Capacitor [capacitance=1µF package="100 mil [THT, electrolytic]"]

nets:
  N1: 74HC595.Q1, R26.Pin_1
  N2: 74HC595.Q2, R17.Pin_1
  N3: 74HC595.Q3, R16.Pin_1
  N4: 74HC595.Q4, R18.Pin_1
  N5: 74HC595.Q5, R20.Pin_1
  N6: 74HC595.Q6, R19.Pin_1
  N7: 74HC595.Q7, R43.Pin_1
  GND: 74HC595.GND, 74HC595.OE, 74HC595_2.GND, 74HC595_2.OE, J2.pin1, 74HC595_3.GND, 74HC595_3.OE, 1uF.-
  5V: 74HC595.MR, 74HC595.VCC, LED7.common_anode, LED5.common_anode, LED6.common_anode, LED4.common_anode, 74HC595_2.MR, 74HC595_2.VCC, LED2.common_anode, LED3.common_anode, LED1.common_anode, J2.pin2, 74HC595_3.MR, 74HC595_3.VCC, LED8.common_anode
  N8: 74HC595.SH_CP, 74HC595_2.SH_CP, jumper.pin2, 74HC595_3.SH_CP
  N9: 74HC595.ST_CP, 74HC595_2.ST_CP, jumper.pin1, 74HC595_3.ST_CP, 1uF.+
  N10: 74HC595.DS, 74HC595_3.Q7'
  N11: 74HC595.Q0, R32.Pin_1
  N12: LED7.red_cathode, R18.Pin_0
  N13: LED7.blue_cathode, R16.Pin_0
  N14: LED7.green_cathode, R17.Pin_0
  N15: R19.Pin_0, LED8.blue_cathode
  N16: R20.Pin_0, LED8.green_cathode
  N17: R43.Pin_0, LED8.red_cathode
  N18: R25.Pin_0, LED4.blue_cathode
  N19: R25.Pin_1, 74HC595_3.Q2
  N20: R26.Pin_0, LED6.red_cathode
  N21: R27.Pin_0, LED5.green_cathode
  N22: R27.Pin_1, 74HC595_3.Q4
  N23: R28.Pin_0, LED5.red_cathode
  N24: R28.Pin_1, 74HC595_3.Q6
  N25: R29.Pin_0, LED6.green_cathode
  N26: R29.Pin_1, 74HC595_3.Q7
  N27: R30.Pin_0, LED4.red_cathode
  N28: R30.Pin_1, 74HC595_3.Q3
  N29: R31.Pin_0, LED4.green_cathode
  N30: R31.Pin_1, 74HC595_3.Q1
  N31: R32.Pin_0, LED6.blue_cathode
  N32: R33.Pin_0, LED5.blue_cathode
  N33: R33.Pin_1, 74HC595_3.Q5
  N34: 74HC595_2.Q1, R38.Pin_1
  N35: 74HC595_2.Q2, R35.Pin_1
  N36: 74HC595_2.Q3, R40.Pin_1
  N37: 74HC595_2.Q4, R34.Pin_1
  N38: 74HC595_2.Q5, R36.Pin_1
  N39: 74HC595_2.Q6, R37.Pin_1
  N40: 74HC595_2.Q7, R39.Pin_1
  N41: 74HC595_2.Q7', 74HC595_3.DS
  N42: 74HC595_2.DS, jumper.pin3
  N43: 74HC595_2.Q0, R41.Pin_1
  N44: R34.Pin_0, LED2.blue_cathode
  N45: R35.Pin_0, LED1.red_cathode
  N46: R36.Pin_0, LED2.red_cathode
  N47: R37.Pin_0, LED3.green_cathode
  N48: R38.Pin_0, LED1.blue_cathode
  N49: R39.Pin_0, LED3.blue_cathode
  N50: R40.Pin_0, LED2.green_cathode
  N51: R41.Pin_0, LED1.green_cathode
  N52: R42.Pin_0, LED3.red_cathode
  N53: R42.Pin_1, 74HC595_3.Q0

notes:
  +5V
  GND
  Q0
  Vcc
  DS
  OE
  ST-CP
  CH-CP
  Q1
  Q2
  Q3
  Q4
  Q5
  Q6
  Q7
  MR
  Q7'
  Data
  Latch
  Clock
